# Fritzing sketch pantalla_i2c (saved by Fritzing 0.9.3b)

parts:
  Componente1 = Arduino Uno (Rev3)
  Componente2 = LCD1602-I2C

nets:
  N1: Componente1.A4/SDA, Componente2.SDA
  N2: Componente1.A5/SCL, Componente2.SCL
  5V: Componente1.5V, Componente2.VCC
  GND: Componente1.GND, Componente2.GND

custom parts:
  LCD1602-I2C: A standard character display, usually with 2x16 characters. Comes in many colors with LCM1602 IIC attached.
